# Fritzing sketch skemarangkaian (saved by Fritzing 0.9.3b)
breadboards: 1

parts:
  Futaba_S3003_Servo = Basic Servo
  DC_Power_Supply = DC Power [voltage=5]
  DC_Power_Supply_2 = DC Power [voltage=5]
  DM542_Driver = Pololu A4988 [package=SO16]
  Stepper_Motor = Stepper Motor - Bipolar
  Arduino_Uno = Arduino Uno (Rev3)

nets:
  GND: Futaba_S3003_Servo.gnd, DC_Power_Supply_2.V-, DM542_Driver.GND#14, Arduino_Uno.GND
  N1: Futaba_S3003_Servo.vcc, DC_Power_Supply_2.V+
  N2: Futaba_S3003_Servo.pulse, Arduino_Uno.D9_PWM
  N3: DC_Power_Supply.V+, DM542_Driver.VDD
  N4: DC_Power_Supply.V-, DM542_Driver.GND#8
  N5: DM542_Driver.STEP, Arduino_Uno.D10_PWM/SS
  N6: DM542_Driver.DIR, Arduino_Uno.D11_PWM/MOSI
  N7: DM542_Driver.1B, Stepper_Motor.B
  N8: DM542_Driver.1A, Stepper_Motor.A
  N9: DM542_Driver.2A, Stepper_Motor.C
  N10: DM542_Driver.2B, Stepper_Motor.D
